# Fritzing sketch LightGary (saved by Fritzing 0.9.2b)
circuit board: 17.0429cm x 8.56423cm
breadboards: 2

parts:
  Bauteil1 = Arduino Uno (Rev3)
  SW1 = ENCODER_RGB_CA [package=encoder_led_3]  # not connected
  LED1 = RGB LED - (4 legs) [package="5 mm [THT]"]
  ENCODER1 = Rotary Encoder with Knob  # not connected
  U1 = 74HC595 [package="DIP16 [THT]"]
  RTC1 = DS1307 RTC Breakout
  U2 = 74HC595 [package="DIP16 [THT]"]
  U3 = 74HC595 [package="DIP16 [THT]"]
  R2 = Resistor [tolerance=±2% resistance=270 package=THT]
  R3 = Resistor [tolerance=±2% resistance=270 package=THT]
  R5 = Resistor [tolerance=±2% resistance=270 package=THT]
  R6 = Resistor [tolerance=±2% resistance=270 package=THT]
  R7 = Resistor [tolerance=±2% resistance=270 package=THT]
  R8 = Resistor [tolerance=±2% resistance=270 package=THT]
  R9 = Resistor [tolerance=±2% resistance=270 package=THT]
  R10 = Resistor [tolerance=±2% resistance=270 package=THT]
  R11 = Resistor [tolerance=±2% resistance=270 package=THT]
  C1 = Electrolytic Capacitor [capacitance=1mF package="100 mil [THT, electrolytic]"]
  J1 = female pin header, 8 pins [form="♀ (female)"]
  J3 = female pin header, 8 pins [form="♀ (female)"]
  R15 = Resistor [tolerance=±2% resistance=270 package=THT]
  R16 = Resistor [tolerance=±2% resistance=270 package=THT]
  R17 = Resistor [tolerance=±2% resistance=330 package=THT]
  R18 = Resistor [tolerance=±2% resistance=330 package=THT]
  R19 = Resistor [tolerance=±2% resistance=330 package=THT]

nets:
  N1: Bauteil1.A1, U2.SH_CP, U3.SH_CP
  N2: Bauteil1.A2, U2.ST_CP, U3.ST_CP
  N3: Bauteil1.A3, U2.DS
  VCC: Bauteil1.5V, LED1.common_anode, U1.MR, U1.VCC, RTC1.5V, U2.MR, U2.VCC, U3.MR, U3.VCC, C1.+
  GND: Bauteil1.GND, U1.GND, U1.OE, RTC1.GND, U2.GND, U2.OE, U3.GND, U3.OE, C1.-
  N4: LED1.red_cathode, R17.Pin_1
  N5: LED1.green_cathode, R18.Pin_1
  N6: LED1.blue_cathode, R19.Pin_1
  N7: U2.Q1, J3.pin2
  N8: U2.Q2, J3.pin3
  N9: U2.Q3, J3.pin4
  N10: U2.Q4, J3.pin5
  N11: U2.Q5, R16.Pin_0
  N12: U2.Q6, R15.Pin_0
  N13: U2.Q7, R3.Pin_0
  N14: U2.Q7', U3.DS
  N15: U2.Q0, J3.pin1
  N16: U3.Q1, R2.Pin_0
  N17: U3.Q2, R9.Pin_0
  N18: U3.Q3, R8.Pin_0
  N19: U3.Q4, R7.Pin_0
  N20: U3.Q5, R6.Pin_0
  N21: U3.Q6, R5.Pin_0
  N22: U3.Q7, R11.Pin_1
  N23: U3.Q0, R10.Pin_1
  N24: R2.Pin_1, J1.pin2
  N25: R3.Pin_1, J3.pin8
  N26: R5.Pin_1, J1.pin7
  N27: R6.Pin_1, J1.pin6
  N28: R7.Pin_1, J1.pin5
  N29: R8.Pin_1, J1.pin4
  N30: R9.Pin_1, J1.pin3
  N31: R10.Pin_0, J1.pin1
  N32: R11.Pin_0, J1.pin8
  N33: J3.pin6, R16.Pin_1
  N34: J3.pin7, R15.Pin_1

custom parts:
  Rotary Encoder with Knob: Rotary Encoder with 1/4" Shaft and Knob
  DS1307 RTC Breakout: DS1307 Real-time Clock Breakout Board with Battery
